# Fritzing sketch AutoTerra (saved by Fritzing 0.9.5d)
perfboards: 1
stripboards: 2

parts:
  R1 = Resistor [tolerance=±5% resistance=220 package=THT]
  Bauteil2 = Arduino Nano 33 IOT
  R4 = Resistor [tolerance=±5% resistance=22 package=THT]
  R5 = Temperature Sensor (Thermistor) [thermistor_type=NTC package=THT]
  R6 = Resistor [tolerance=±5% resistance=10k package=THT]
  ZS-042_RTC1 = ZS-042 RTC Module
  SHT45 = Humidity Temperature Sensor SHT15
  Pumpenrelais = Relay [part_number=FRS1B-S package=THT]
  U1 = Voltage Regulator - 5V [package="DPak [SMD]"]
  U2 = Voltage Regulator - 3.3V [package="TO220 [THT]"]
  R7 = Resistor [tolerance=±5% resistance=10k package=THT]
  R8 = Resistor [tolerance=±5% resistance=10k package=THT]
  C1 = Ceramic Capacitor [capacitance=1mF package="100 mil [THT, multilayer]"]
  2N3904 = NPN-Transistor [package="TO92 [THT]"]
  R9 = Resistor [tolerance=±5% resistance=10k package=THT]
  R10 = Resistor [tolerance=±5% resistance=2.2k package=THT]
  R11 = Resistor [tolerance=±5% resistance=2.2k package=THT]
  LED1 = LED - 3mm [color="Infrared (940nm)" package="3 mm [THT]"]
  IR = female pin header, 2 pins [form="♀ (female)"]
  IR-Header = male pin header, 2 pins [form="♂ (male)"]
  Fan2 = male pin header, 4 pins [form="♂ (male)"]
  Fan1 = male pin header, 4 pins [form="♂ (male)"]
  Liquid_Sensor = male pin header, 3 pins [form="♂ (male)"]
  TCS34725FN = male pin header, 6 pins [form="♂ (male)"]
  ToNTC = male pin header, 2 pins [form="♂ (male)"]
  NTC = female pin header, 2 pins [form="♀ (female)"]
  J1 = female pin header, 15 pins [form="♀ (female)"]
  J2 = female pin header, 15 pins [form="♀ (female)"]
  ToSHT = male pin header, 4 pins [form="♂ (male)"]
  ToDS3231/AT24C32 = male pin header, 6 pins [form="♂ (male)"]
  FromSHT = female pin header, 4 pins [form="♀ (female)"]
  FromDS3231/AT24C32 = female pin header, 6 pins [form="♀ (female)"]
  3_3Vin = male pin header, 2 pins [form="♂ (male)"]
  3_3Vout = female pin header, 2 pins [form="♀ (female)"]
  5Vout = female pin header, 2 pins [form="♀ (female)"]
  5Vin = male pin header, 2 pins [form="♂ (male)"]
  Vin = male pin header, 2 pins [form="♂ (male)"]

nets:
  N1: R1.Pin_0, Bauteil2.D3~, J2.pin6
  N2: R1.Pin_1, IR-Header.pin1
  N3: Bauteil2.RX, J2.pin1
  N4: Bauteil2.TX, J2.pin2
  N5: Bauteil2.RESET, Bauteil2.A7, J1.pin11, J1.pin13, J2.pin3
  N6: Bauteil2.D2, J2.pin5, ToDS3231/AT24C32.pin5
  N7: Bauteil2.D4, TCS34725FN.pin1, J2.pin7
  N8: Bauteil2.D5~, Liquid_Sensor.pin1, J2.pin8
  N9: Bauteil2.D6~, R10.Pin_0, J2.pin9
  N10: Bauteil2.D7, TCS34725FN.pin2, J2.pin10
  N11: Bauteil2.D8, J2.pin11, ToDS3231/AT24C32.pin6
  N12: Bauteil2.D9~, R8.Pin_0, Fan1.pin3, J2.pin12
  N13: Bauteil2.D10~, R7.Pin_1, Fan2.pin3, J2.pin13
  N14: Bauteil2.D11/MOSI, Pumpenrelais.B, J2.pin14
  N15: Bauteil2.D12~/MISO, J2.pin15
  N16: Bauteil2.VIN, J1.pin15, Vin.pin1
  GND: Bauteil2.GND, Bauteil2.D13~, Pumpenrelais.A, Pumpenrelais.COIL1, C1.0, 2N3904.E, R9.Pin_1, IR-Header.pin2, Fan2.pin1, Fan1.pin1, Liquid_Sensor.pin3, TCS34725FN.pin5, ToNTC.pin2, J1.pin1, J1.pin14, J2.pin4, ToSHT.pin2, ToDS3231/AT24C32.pin1, 3_3Vin.pin1, 5Vin.pin2
  N17: Bauteil2.A6, J1.pin10
  N18: Bauteil2.A5, TCS34725FN.pin3, J1.pin9, ToSHT.pin3, ToDS3231/AT24C32.pin4
  N19: Bauteil2.A4, TCS34725FN.pin4, J1.pin8, ToSHT.pin4, ToDS3231/AT24C32.pin3
  N20: Bauteil2.A3, J1.pin7
  N21: Bauteil2.A2, J1.pin6
  N22: Bauteil2.A1, J1.pin5
  N23: Bauteil2.A0, R6.Pin_1, ToNTC.pin1, J1.pin4
  N24: Bauteil2.AREF, J1.pin3
  N25: Bauteil2.3V3, J1.pin2
  N26: R4.Pin_0, R6.Pin_0
  N27: R4.Pin_1, Pumpenrelais.COIL2, R7.Pin_0, R8.Pin_1, Liquid_Sensor.pin2, TCS34725FN.pin6, ToSHT.pin1, ToDS3231/AT24C32.pin2, 3_3Vin.pin2
  N28: R5.pin_0, NTC.pin2
  N29: R5.pin_1, NTC.pin1
  N30: ZS-042_RTC1.GND, FromDS3231/AT24C32.pin1
  N31: ZS-042_RTC1.VCC, FromDS3231/AT24C32.pin2
  N32: ZS-042_RTC1.SDA, FromDS3231/AT24C32.pin3
  N33: ZS-042_RTC1.SCL, FromDS3231/AT24C32.pin4
  N34: ZS-042_RTC1.SQW, FromDS3231/AT24C32.pin5
  N35: ZS-042_RTC1.32K, FromDS3231/AT24C32.pin6
  N36: SHT45.GND, FromSHT.pin2
  N37: SHT45.SCL, FromSHT.pin3
  N38: SHT45.SDA, FromSHT.pin4
  N39: SHT45.VCC, FromSHT.pin1
  24V: U1.input_voltage, U2.input_voltage
  GND_2: U1.GND, U2.GND, 3_3Vout.pin1, 5Vout.pin2
  N40: U1.output_voltage, 5Vout.pin1
  N41: U2.output_voltage, 3_3Vout.pin2
  N42: C1.1, R11.Pin_1, Fan2.pin2, Fan1.pin2, 5Vin.pin1, Vin.pin2
  N43: 2N3904.B, R9.Pin_0, R10.Pin_1
  N44: 2N3904.C, R11.Pin_0, Fan2.pin4, Fan1.pin4
  N45: LED1.cathode, IR.pin2
  N46: LED1.anode, IR.pin1

custom parts:
  Arduino Nano 33 IOT: The Arduino Nano 33 IoT is the easiest and cheapest point of entry to enhance existing devices (and creating new ones) to be part of the IoT and designing pico-network applications. Whether you are looking at building a sensor network connected to your office or home router, or if you want to create a BLE device sending data to a cellphone, the Nano 33 IoT is your one-stop-solution for many of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

// code stored in the sketch: IR_Tag.ino
/*
 * SimpleSender.cpp
 *
 *  Demonstrates sending IR codes in standard format with address and command
 *  An extended example for sending can be found as SendDemo.
 *  Sending IR codes using several pins for sending is implements in the MultipleSendPins example.
 *
 *  Copyright (C) 2020-2025  Armin Joachimsmeyer
 *  armin.joachimsmeyer@gmail.com
 *
 *  This file is part of Arduino-IRremote https://github.com/Arduino-IRremote/Arduino-IRremote.
 *
 *  MIT License
 * Ja und zwar so, wie ich weiter oben (in meiner Antwort, die mit "Ja, das brauche ich." startet) beschrieben habe
 */
// USED LIBRARIES
#include <Arduino.h>
#include <RTClib.h>
#include <IRremote.h>

// Needed for Libraries
#if !defined(ARDUINO_ESP32C3_DEV)  // This is due to a bug in RISC-V compiler, which requires unused function sections :-(.
#define DISABLE_CODE_FOR_RECEIVER  // Disables static receiver code like receive timer ISR handler and static IRReceiver and irparams data. Saves 450 bytes program memory and 269 bytes RAM if receiving functions are not required.
#endif
#define NO_LED_FEEDBACK_CODE  // Saves 216 bytes program memory
#include "PinDefinitionsAndMore.h"
#include <IRremote.hpp>  // include the library

// My Things
struct Preset {
  uint8_t R, G, B, W;  // Werte 0–10, direkt wie TerraSky-Stufen
  uint8_t pres;       // Preset-Taste zum Bestätigen
};
struct alarmEvent {
  uint8_t phaseHour, phaseMinute;  // Preset Zeit
  uint8_t alarmPreset;            // Welches Preset soll zum Alarm aufgerufen werden
};
RTC_DS3231 rtc;
IRsend irsend;
bool ERROR = false;
bool DEBUG = true;

// My Defines
int IR_PIN = 3;
int MAX_STEPS = 10;               // maximale Stufenzahl pro Farbe (TerraSky hat 10 Stufen)
const uint8_t fadeMinutes = 30;  // Fade-Dauer in Minuten pro Übergang


uint8_t rAddress = 0x4;
uint8_t sRepeats = 0;
uint8_t sPOWER = 0x40;
uint8_t sSTART = 0x44;
uint8_t sROTm = 0x50;
uint8_t sROTp = 0x54;
uint8_t sGRUNm = 0x51;
uint8_t sGRUNp = 0x55;
uint8_t sBLAUm = 0x4D;
uint8_t sBLAUp = 0x49;
uint8_t sWEISSm = 0x4C;
uint8_t sWEISSp = 0x48;
uint8_t sP1 = 0x1C;
uint8_t sP2 = 0x1D;
uint8_t sP3 = 0x1E;
uint8_t sP4 = 0x1F;
uint8_t sMONDw = 0x18;
uint8_t sMONDm = 0x19;
uint8_t sMONDv = 0x1A;
uint8_t sRISE = 0x1B;
uint8_t sWOLKEl = 0x14;
uint8_t sWOLKEe = 0x15;
uint8_t sWOLKEm = 0x16;
uint8_t sWOLKEv = 0x17;
uint8_t sGEWITTERstark = 0x10;
uint8_t sGEWITTERl = 0x11;
uint8_t sGEWITTERsonnig = 0x12;
uint8_t sFARBZYKLUS = 0x13;
uint8_t sROT = 0x5C;
uint8_t sBLAUh = 0x5D;
uint8_t sLILA = 0x41;
uint8_t sWEISS = 0x58;
uint8_t sGELB = 0x59;
uint8_t sBLAU = 0x45;

// Welche Presets hast du gespeichert?
enum PresNames {
  status,  // Zwischenspeicher für Übergänge
  Morgen,
  Vormittag,
  Mittag,
  Nacht,
  Halbmond
};

const int pNum = sizeof(PresNames) / sizeof(PresNames[0]);

// Reihenfolge R, G, B, W, Remote-Befehl
Preset presets[] = {
  { 0, 0, 0, 0, sP4 },    // Zwischenspeicher/Status, Befehl wird nicht genutzt
  { 1, 1, 1, 4, sP1 },    // Morgen
  { 1, 3, 1, 6, sP2 },    // Vormittag
  { 1, 4, 1, 8, sP3 },    // Mittag
  { 0, 1, 2, 1, sP4 },    //Nacht
  { 0, 0, 4, 0, sMONDm }  // Halbmond
};

// Zeitplan
const int aNum = 10;
alarmEvent myPhases[aNum] = {
  { 7, 0, presets[Morgen].pres },
  { 8, 0, presets[Vormittag].pres },
  { 11, 37, presets[Nacht].pres },
  { 11, 38, presets[Mittag].pres },
  { 11, 39, presets[Nacht].pres },
  { 11, 40, presets[Mittag].pres },
  { 12, 0, presets[Mittag].pres },
  { 15, 0, presets[Vormittag].pres },
  { 19, 0, presets[Morgen].pres },
  { 20, 30, presets[Halbmond].pres }
};

// ==== Variablen ====
uint8_t currentPhase = 0;
unsigned long lastFadeTime = 0;
bool fading = false;

// ==== Hilfsfunktionen ====

void sendCommand(uint8_t cmd) {
  IrSender.sendNEC(rAddress, cmd, sRepeats);
  Serial.println();
  /*Serial.print(F("Send now: address=0x"));
  Serial.print(rAddress, HEX);
  Serial.print(F(", command=0x"));
  Serial.print(cmd, HEX);
  Serial.print(F(", repeats="));
  Serial.print(sRepeats);
  Serial.println();

  Serial.println(F("Send standard NEC with 8 bit address"));
  Serial.flush();*/
  delay(1000);  // kleine Pause zwischen Signalen
  /*for (int t = 0; t <= 4; t++) {
    IrSender.sendNEC(rAddress, cmd, sRepeats);
    //Serial.println();
    //Serial.println(sRepeats);
    sRepeats++;
    delay(1000);
  }
  sRepeats = 0;*/
}

DateTime constrTime(int alarmNumber, DateTime runTime) {
  // DateTime now = rtc.now();
  DateTime constructTime(runTime.year(), runTime.month(), runTime.day(), myPhases[alarmNumber].phaseHour, myPhases[alarmNumber].phaseMinute, 0);
  if (!constructTime.isValid()) {
    if (DEBUG) {
      //Serial.println("Timeformat Error");
    }
    ERROR = true;
  }
  return constructTime;
}

// ==== Setup & Loop ====

void setup() {

  //Serial.begin(115200);
  /*
  // Just to know which program is running on my Arduino
  Serial.println(F("START " __FILE__ " from " __DATE__ "\r\nUsing library version " VERSION_IRREMOTE));
  Serial.print(F("Send IR signals at pin "));
  Serial.println(IR_SEND_PIN);

  /*
   * No IR library setup required :-)
   * Default is to use IR_SEND_PIN -which is defined in PinDefinitionsAndMore.h- as send pin
   * and use feedback LED at default feedback LED pin if not disabled by #define NO_LED_SEND_FEEDBACK_CODE
   */
  irsend.begin(IR_PIN);
  if (!rtc.begin()) {
    /*Serial.println("Couldn't find RTC");
    Serial.flush();
    while (1) delay(10);*/
  } /*
  if (!rtc.isrunning()) {
    Serial.println("RTC is NOT running, let's set the time!");
    // When time needs to be set on a new device, or after a power loss, the
    // following line sets the RTC to the date & time this sketch was compiled
    rtc.adjust(DateTime(F(__DATE__), F(__TIME__)));
  }*/
  DateTime setTime = rtc.now();
  //Serial.println(String("DateTime::TIMESTAMP_FULL:\t") + setTime.timestamp(DateTime::TIMESTAMP_FULL));
}

void loop() {
  DateTime now = rtc.now();
  for (int i = 0; i < aNum; i++) {
    DateTime testTime(constrTime(i, now));
    if (testTime == now) {
      sendCommand(myPhases[i].alarmPreset);
    }
  }
  delay(300);
}
